// Logisim project dunceputerlogic.circ as structural Verilog: 1 circuit, main circuit main
module main (
  input  clock,
  output [7:0] out_2
);

  wire and_1_out, and_2_out, and_3_out, and_4_out, counter_1_carry, not_1_out, not_2_out, not_3_out,
       or_1_out, or_2_out, or_3_out, ram_1_dout, register_1_q;
  wire [4:0] rom_1_data;
  wire [7:0] counter_1_q;

  Counter counter_1 (
    .clr(counter_1_carry), .load(and_3_out), .up(1'b1), .clk(clock), .D(out_2), .carry(counter_1_carry),
    .Q(counter_1_q));  // open: count
  ROM #(.dataWidth(13)) rom_1 (.addr(counter_1_q), .data({out_2, rom_1_data}));
  RAM #(.clearpin("true"), .dataWidth(1), .trigger("falling")) ram_1 (
    .addr(out_2), .we(rom_1_data[2]), .oe(not_1_out), .clk(clock), .din(and_1_out), .dout(ram_1_dout),
    .clr(rom_1_data[4]));
  not not_1 (not_1_out, rom_1_data[2]);
  and and_1 (and_1_out, rom_1_data[2], or_1_out);
  or or_1 (or_1_out, out_2[0], register_1_q);
  or or_2 (or_2_out, rom_1_data[0], rom_1_data[1]);
  and and_2 (and_2_out, ram_1_dout, rom_1_data[1]);
  Register #(.width(1)) register_1 (.D(or_3_out), .en(or_2_out), .clk(clock), .Q(register_1_q), .clr(rom_1_data[4]));
  or or_3 (or_3_out, and_2_out, and_4_out);
  and and_3 (and_3_out, rom_1_data[3], not_3_out);
  not not_2 (not_2_out, register_1_q);
  and and_4 (and_4_out, not_2_out, rom_1_data[0]);
  not not_3 (not_3_out, register_1_q);

  // Notes on the sheet:
  //   manual for debuging
  //   carry pin resets counter to 0
  //   contents of rom_1 (hex, n*v repeats v):
  //   0 44 42 1 8 10
  //   clears RAM with RST instruction
  //   instructions that write to RAM
  //   0-4 opcode
  //   5-12 operand
  //   instructions that write to acc
  //   set acc to inverted value
  //   if INV is run
  //   |
  //   V
  //   reset acc on RST
  //   if acc==0 & the current instruction is JNZ;
  //   jump to the instruction in the operand
  //   main bus (accumulator value)
endmodule
